# Fritzing sketch Arduino_UPS (saved by Fritzing 0.9.3b)
breadboards: 1

parts:
  Part1 = LCD Keypad Shield
  Part2 = Arduino Uno (Rev3)
  Q1 = Basic FET N-Channel [package="D2Pak [SMD]"]
  12V_7Ah_Pb_battery = Battery Holders [package=lipo-1100mAh]
  R1 = Resistor [tolerance=±5% resistance=2.2k package="2010 [SMD]"]
  R2 = Resistor [tolerance=±5% resistance=20k package="0603 [SMD]"]
  R3 = Resistor [tolerance=±5% resistance=220 package="0603 [SMD]"]
  F1 = Resettable Fuse PTC [package=ptc]
  J1 = Piezo Speaker

nets:
  N1: Part1.A1, R2.Pin_1, R3.Pin_0
  N2: Part1.D11_MOSI, Part2.D4
  N3: Part1.D12_MISO, Part2.D5_PWM
  N4: Part1.D13_SCK, Part2.D6_PWM
  N5: Part1.D0_RX, Part2.D0/RX
  N6: Part1.D1_TX, Part2.D1/TX
  N7: Part1.D2, Part2.D2
  N8: Part1.D3, Part2.D3_PWM, R1.Pin_0
  N9: Part1.GND, Q1.source, 12V_7Ah_Pb_battery.-, R3.Pin_1
  N10: Q1.Gate, R1.Pin_1
  N11: Q1.drain, J1.pin1
  N12: 12V_7Ah_Pb_battery.+, R2.Pin_0, F1.1, F1.2, J1.pin2

custom parts:
  LCD Keypad Shield: It consists of a 1602 white character blue backlight LCD. The keypad consists of 5 keys — select, up, right, down and left. To save the digital IO pins, the keypad interface uses only one ADC channel. The key value is read through a 5 stage voltage divider.
