# Fritzing sketch Arduino_UPS (saved by Fritzing 0.9.3b)
breadboards: 2

parts:
  Part1 = LCD Keypad Shield
  Part2 = Arduino Uno (Rev3)
  Q1 = Basic FET N-Channel [package="D2Pak [SMD]"]
  12V_7Ah_Pb_battery = Battery Holders [package=lipo-1100mAh]
  R3 = Resistor [tolerance=±5% resistance=2.2k package="2010 [SMD]"]
  R1 = Resistor [tolerance=±5% resistance=20k package="0603 [SMD]"]
  R2 = Resistor [tolerance=±5% resistance=10k package="0603 [SMD]"]
  F1 = Resettable Fuse PTC [package=ptc]
  12V_piezo_speaker = Piezo Speaker
  F2 = Resettable Fuse PTC [package=ptc]
  Input_12V_DC = Power Jack [package=power_jack_pth_lock]
  Output_12V_DC = Power Jack [package=power_jack_pth_lock]

nets:
  N1: Part1.A1, R1.Pin_1, R2.Pin_0
  N2: Part1.D11_MOSI, Part2.D4
  N3: Part1.D12_MISO, Part2.D5_PWM
  N4: Part1.D13_SCK, Part2.D6_PWM
  N5: Part1.D0_RX, Part2.D0/RX
  N6: Part1.D1_TX, Part2.D1/TX
  N7: Part1.D2, Part2.D2
  N8: Part1.D3, Part2.D3_PWM, R3.Pin_0
  GND: Part1.GND, Q1.source, 12V_7Ah_Pb_battery.-, R2.Pin_1, Input_12V_DC.GND, Output_12V_DC.GND
  N9: Q1.Gate, R3.Pin_1
  N10: Q1.drain, 12V_piezo_speaker.pin1
  N11: 12V_7Ah_Pb_battery.+, F2.1, Input_12V_DC.PWR, Output_12V_DC.PWR
  N12: R1.Pin_0, F1.2, F2.2
  N13: F1.1, 12V_piezo_speaker.pin2

custom parts:
  LCD Keypad Shield: It consists of a 1602 white character blue backlight LCD. The keypad consists of 5 keys — select, up, right, down and left. To save the digital IO pins, the keypad interface uses only one ADC channel. The key value is read through a 5 stage voltage divider.
