# Fritzing sketch Voltage_divider (saved by Fritzing 0.9.3b)
breadboards: 1

parts:
  R1 = Resistor [tolerance=±5% resistance=20k package="0603 [SMD]"]
  R2 = Resistor [tolerance=±5% resistance=10k package="0603 [SMD]"]

nets:
  N1: R1.Pin_1, R2.Pin_0

notes:
  Battery 12V DC
  - +
  Arduino analog input pin 1
